# Fritzing sketch Arduino4Bio-EnviroDataLogger (saved by Fritzing 0.8.7b)
circuit board: 8.46667cm x 5.64444cm
breadboards: 1

parts:
  Part1 = Arduino Ethernet Shield (Rev3)
  IC1 = DS1307 [package=THT]
  Y1 = CRYSTAL [package=crystal-32khz-smd_epson_mc146]
  BAT1 = Battery Holders [package=battcon_12mm]
  RHT1 = Humidity and Temperature Sensor RHT03
  R1 = Resistor [tolerance=±5% resistance=220 package=THT]
  LED1 = LED - 5mm [color="Red (633nm)" package="5 mm [THT]"]

nets:
  N1: Part1.PWM_D9, R1.Pin_0
  N2: Part1.GND, IC1.0V, BAT1.-, RHT1.GND_2, LED1.cathode
  N3: Part1.A4/SDA, IC1.SDA_-_I2C_Data
  N4: Part1.A5/SCL, IC1.SCL_-_I2C_Clock
  N5: Part1.D2, RHT1.Data-signal
  5V: Part1.5V, IC1.+V, RHT1.Vcc
  N6: IC1.X1_-_Crystal, Y1.1
  N7: IC1.X2_-_Crystal, Y1.2
  N8: IC1.Vbat_-_Backup_Supply, BAT1.+
  N9: R1.Pin_1, LED1.anode
